// Logisim project banc_registre.circ as structural Verilog: 1 circuit, main circuit main
module main (
  input  [31:0] DataIn,
  input  [2:0] RegDest,
  input  Clk,
  input  Reset,
  input  [2:0] RegA,
  input  [2:0] RegB,
  output [31:0] R0,
  output [31:0] A,
  output [31:0] R1,
  output [31:0] B,
  output [31:0] R2,
  output [31:0] R3,
  output [31:0] R4,
  output [31:0] R5,
  output [31:0] R6,
  output [31:0] R7
);

  wire d0, d1, d2, d3, d4, d5, d6, d7;

  Decoder #(.select(3), .enable("false")) decoder_1 (
    .out0(d0), .out1(d1), .out2(d2), .out3(d3), .out4(d4), .out5(d5), .out6(d6), .out7(d7), .sel(RegDest));
  Register #(.width(32), .trigger("high")) u_R0 (.D(DataIn), .en(d0), .Q(R0), .clk(Clk), .clr(Reset));
  Register #(.width(32), .trigger("high")) u_R1 (.D(DataIn), .en(d1), .Q(R1), .clk(Clk), .clr(Reset));
  Register #(.width(32), .trigger("high")) u_R2 (.D(DataIn), .en(d2), .Q(R2), .clk(Clk), .clr(Reset));
  Register #(.width(32), .trigger("high")) u_R3 (.D(DataIn), .en(d3), .Q(R3), .clk(Clk), .clr(Reset));
  Register #(.width(32), .trigger("high")) u_R4 (.D(DataIn), .en(d4), .Q(R4), .clk(Clk), .clr(Reset));
  Register #(.width(32), .trigger("high")) u_R5 (.D(DataIn), .en(d5), .Q(R5), .clk(Clk), .clr(Reset));
  Register #(.width(32), .trigger("high")) u_R6 (.D(DataIn), .en(d6), .Q(R6), .clk(Clk), .clr(Reset));
  Register #(.width(32), .trigger("high")) u_R7 (.D(DataIn), .en(d7), .Q(R7), .clk(Clk), .clr(Reset));
  Multiplexer #(.select(3), .width(32), .enable("false")) multiplexer_1 (
    .in0(R0), .in1(R1), .in2(R2), .in3(R3), .in4(R4), .in5(R5), .in6(R6), .in7(R7), .out(A), .sel(RegA));
  Multiplexer #(.select(3), .width(32), .enable("false")) multiplexer_2 (
    .in0(R0), .in1(R1), .in2(R2), .in3(R3), .in4(R4), .in5(R5), .in6(R6), .in7(R7), .out(B), .sel(RegB));

  // Notes on the sheet:
  //   Entrées
  //   Décodeur
  //   (Pour enable un des 8 registres)
  //   Registres
  //   Sorties registres
  //   Sorties A et B
endmodule
