// Logisim project machine.circ as structural Verilog: 2 circuits, main circuit main
module main (
);

  wire clock_1_out, cpu_1_store, Rst_Button_out;
  wire [7:0] RAM_Addr, ROM_Addr;
  wire [15:0] bit_extender_1_out;
  wire [31:0] cpu_1_r0, cpu_1_r1, cpu_1_r2, cpu_1_r3, cpu_1_r4, cpu_1_r5, cpu_1_r6, cpu_1_r7, cpu_1_ram_out,
       ram_1_data, rom_1_data;
  wire [31:8] cpu_1_ram_addr;

  RAM #(.dataWidth(32), .bus("separate")) ram_1 (
    .addr(RAM_Addr), .din(cpu_1_ram_out), .data(ram_1_data), .str(cpu_1_store), .clk(clock_1_out), .ld(1'b1),
    .clr(Rst_Button_out));  // open: sel
  Clock clock_1 (.out(clock_1_out));
  LED A0 (.in(ram_1_data[0]));
  LED A1 (.in(ram_1_data[1]));
  LED A3 (.in(ram_1_data[3]));
  LED A2 (.in(ram_1_data[2]));
  Button Clk_Button (.out(clock_1_out));
  Button Rst_Button (.out(Rst_Button_out));
  Bit_Extender #(.in_width(32)) bit_extender_1 (.in(ram_1_data), .out(bit_extender_1_out));
  LED A4 (.in(ram_1_data[4]));
  LED A5 (.in(ram_1_data[5]));
  ROM #(.dataWidth(32)) rom_1 (.addr(ROM_Addr), .data(rom_1_data));  // open: sel
  CPU cpu_1 (
    .RAM_In(rom_1_data), .ROM_In(bit_extender_1_out), .Clk(clock_1_out), .Reset(Rst_Button_out),
    .ROM_Addr(ROM_Addr), .R0(cpu_1_r0), .R4(cpu_1_r4), .RAM_Addr({cpu_1_ram_addr, RAM_Addr}), .R1(cpu_1_r1),
    .R5(cpu_1_r5), .RAM_Out(cpu_1_ram_out), .Store(cpu_1_store), .R2(cpu_1_r2), .R6(cpu_1_r6), .R3(cpu_1_r3),
    .R7(cpu_1_r7));
  LED A6 (.in(ram_1_data[6]));
  LED A7 (.in(ram_1_data[7]));
  LED L0 (.in(cpu_1_r0[0]));
  // Probe on cpu_1_r1
  // Probe on cpu_1_r0
  LED L3 (.in(cpu_1_r0[3]));
  LED L1 (.in(cpu_1_r0[1]));
  LED L2 (.in(cpu_1_r0[2]));
  // Probe on cpu_1_r3
  // Probe on cpu_1_r2
  // Probe on cpu_1_r5
  // Probe on cpu_1_r4
  LED L4 (.in(cpu_1_r0[4]));
  LED L5 (.in(cpu_1_r0[5]));
  // Probe on cpu_1_r7
  // Probe on cpu_1_r6
  LED L6 (.in(cpu_1_r0[6]));
  LED L7 (.in(cpu_1_r0[7]));
  LED LED_1 (.in(RAM_Addr[0]));
  LED LED_2 (.in(RAM_Addr[1]));
  LED LED_3 (.in(RAM_Addr[2]));
  LED LED_4 (.in(RAM_Addr[3]));
  LED LED_5 (.in(RAM_Addr[4]));
  LED LED_6 (.in(RAM_Addr[5]));
  LED LED_7 (.in(RAM_Addr[6]));
  LED LED_8 (.in(RAM_Addr[7]));

  // Notes on the sheet:
  //   Use only 8 bit adresses
endmodule

module CPU (
  input  [31:0] RAM_In,
  input  [15:0] ROM_In,
  input  Clk,
  input  Reset,
  output [7:0] ROM_Addr,
  output [31:0] R0,
  output [31:0] R4,
  output [31:0] RAM_Addr,
  output [31:0] R1,
  output [31:0] R5,
  output [31:0] RAM_Out,
  output Store,
  output [31:0] R2,
  output [31:0] R6,
  output [31:0] R3,
  output [31:0] R7
);

  wire Carry, DP_shift, Imm32_en, Store_t;
  wire [2:0] Rd, Rm, Rn;
  wire [3:0] ALU_opcode, Flags;
  wire [4:0] bitselector_1_out, Imm5, multiplexer_3_out;
  wire [31:0] B, Imm32, multiplexer_1_out, multiplexer_2_out, S;

  Multiplexer #(.width(32), .enable("false")) multiplexer_1 (
    .in0(S), .in1(RAM_In), .out(multiplexer_1_out), .sel(Store));
  // CONTROLEUR controleur_1: pin names not known; wires that end beside it: ROM_In, Flags, Clk, Reset, Carry, DP_shift, Imm32_en, Imm5, Imm32, ALU_opcode, Rm, Rn, Rd, RAM_Addr, Store, Store_t, ROM_Addr
  // BANC_DE_REGISTRE banc_de_registre_1: pin names not known; wires that end beside it: RAM_Out, multiplexer_1_out, B, R0, Clk, R1, Reset, R2, R3, Rd, R4, Rm, R5, Rn, R6, R7
  Multiplexer #(.width(32), .enable("false")) multiplexer_2 (
    .in0(Imm32), .in1(RAM_Out), .out(multiplexer_2_out), .sel(Imm32_en));
  BitSelector #(.width(32), .group(5)) bitselector_1 (.in(RAM_Out), .out(bitselector_1_out), .sel(3'b000));
  Multiplexer #(.width(5), .enable("false")) multiplexer_3 (
    .in0(bitselector_1_out), .in1(Imm5), .out(multiplexer_3_out), .sel(DP_shift));
  // ALU alu_1: pin names not known; wires that end beside it: multiplexer_2_out, B, multiplexer_3_out, Carry, ALU_opcode, S, Flags

  // Other names for the same wires on the sheet: A[31:0] = RAM_Out; Load = Store; PC[7:0] = ROM_Addr
endmodule
